# Fritzing sketch bluphoria_sensor (saved by Fritzing 1.0.2b)
perfboards: 1

parts:
  Part1 = Adafruit Trinket M0 [part_number="Adafruit #3500"]
  NCIR1 = NCIR [package="SIP (Single Inline) [THT]"]
  R1 = TRIMPOT [maximum_resistance=10kΩ knob_status=50% power=0.5W package=trim_pot_pth]
  J1 = female pin header, 2 pins [form="♀ (female)"]
  J2 = female pin header, 2 pins [form="♀ (female)"]
  J3 = female pin header, 2 pins [form="♀ (female)"]
  J4 = female pin header, 2 pins [form="♀ (female)"]
  IC2 = IC, DIP package, 8 pins [chip_label=6N139]
  IC3 = IC, DIP package, 8 pins [chip_label=6N139]
  R4 = Resistor [tolerance=±5% power=0.25W resistance=330 package=THT]
  R5 = Resistor [tolerance=±5% power=0.25W resistance=330 package=THT]
  J5 = female pin header, 2 pins [form="♀ (female)"]
  J6 = female pin header, 2 pins [form="♀ (female)"]

nets:
  GND: Part1.GND, NCIR1.GND, R1.CW, J2.pin2
  N1: Part1.D4_A2_PA06_TXD_MOSI, J1.pin2
  N2: Part1.D3_A3_PA07_RXD_SCK, J1.pin1
  N3: Part1.3.3V, R1.CCW
  N4: Part1.D2_A1_PA09_SCL_MISO, NCIR1.SCL
  N5: Part1.D1_A0_PA02, R1.WIPER
  N6: Part1.D0_A4_PA08_SDA, NCIR1.SDA
  N7: Part1.VBUS, NCIR1.VCC, J2.pin1
  N8: J3.pin1, R4.Pin_0
  N9: J3.pin2, R5.Pin_0
  N10: J4.pin1, IC3.pin8, J5.pin1
  N11: J4.pin2, J6.pin2
  N12: IC2.pin2, R4.Pin_1
  N13: IC2.pin6, J6.pin1
  N14: IC3.pin2, R5.Pin_1
  N15: IC3.pin6, J5.pin2

notes:
  grove connector
  mini DIN connector
  dmx controller connections
  GND
  5V
  button prev "-"
  button next "+"
